// Logisim project 32-bit Processor.circ as structural Verilog
module _8_32_bit_Register_File (
  input  [2:0] rs,
  input  [31:0] Write_Data,
  input  [2:0] rt,
  input  [2:0] rd,
  input  Clock,
  input  Clear,
  input  Write_Control,
  output [31:0] Read_Data_1,
  output [31:0] Read_Data_2
);

  wire and_1_out, and_2_out, and_3_out, and_4_out, and_5_out, and_6_out, and_7_out, and_8_out,
       decoder_1_out0, decoder_1_out1, decoder_1_out2, decoder_1_out3, decoder_1_out4, decoder_1_out5,
       decoder_1_out6, decoder_1_out7;
  wire [31:0] r0_q, r1_q, r2_q, r3_q, r4_q, r5_q, r6_q, r7_q;

  and and_1 (and_1_out, decoder_1_out7, Write_Control);
  Decoder #(.select(3), .enable("false")) decoder_1 (
    .out0(decoder_1_out0), .out1(decoder_1_out1), .out2(decoder_1_out2), .out3(decoder_1_out3),
    .out4(decoder_1_out4), .out5(decoder_1_out5), .out6(decoder_1_out6), .out7(decoder_1_out7), .sel(rd));
  Register #(.width(32)) r7 (.D(Write_Data), .en(and_1_out), .Q(r7_q), .clk(Clock), .clr(Clear));
  and and_2 (and_2_out, decoder_1_out6, Write_Control);
  Register #(.width(32)) r5 (.D(Write_Data), .en(and_3_out), .Q(r5_q), .clk(Clock), .clr(Clear));
  Register #(.width(32)) r6 (.D(Write_Data), .en(and_2_out), .Q(r6_q), .clk(Clock), .clr(Clear));
  and and_3 (and_3_out, decoder_1_out5, Write_Control);
  Register #(.width(32)) r4 (.D(Write_Data), .en(and_4_out), .Q(r4_q), .clk(Clock), .clr(Clear));
  and and_4 (and_4_out, decoder_1_out4, Write_Control);
  Register #(.width(32)) r3 (.D(Write_Data), .en(and_5_out), .Q(r3_q), .clk(Clock), .clr(Clear));
  and and_5 (and_5_out, decoder_1_out3, Write_Control);
  Register #(.width(32)) r2 (.D(Write_Data), .en(and_6_out), .Q(r2_q), .clk(Clock), .clr(Clear));
  and and_6 (and_6_out, decoder_1_out2, Write_Control);
  and and_7 (and_7_out, decoder_1_out1, Write_Control);
  Register #(.width(32)) r1 (.D(Write_Data), .en(and_7_out), .Q(r1_q), .clk(Clock), .clr(Clear));
  and and_8 (and_8_out, decoder_1_out0, Write_Control);
  Register #(.width(32)) r0 (.D(Write_Data), .en(and_8_out), .Q(r0_q), .clk(Clock), .clr(Clear));
  Multiplexer #(.select(3), .width(32), .enable("false")) multiplexer_1 (
    .in0(r0_q), .in1(r1_q), .in2(r2_q), .in3(r3_q), .in4(r4_q), .in5(r5_q), .in6(r6_q), .in7(r7_q),
    .out(Read_Data_1), .sel(rs));
  Multiplexer #(.select(3), .width(32), .enable("false")) multiplexer_2 (
    .in0(r0_q), .in1(r1_q), .in2(r2_q), .in3(r3_q), .in4(r4_q), .in5(r5_q), .in6(r6_q), .in7(r7_q),
    .out(Read_Data_2), .sel(rt));
endmodule

module _32_bit_ALU (
  input  [31:0] A,
  input  [31:0] B,
  input  Cin,
  input  Binv,
  input  AluOp,
  output Z,
  output [31:0] AluOut,
  output Cout
);

  wire [31:0] adder_1_out, multiplexer_1_out, nand_1_out, not_1_out;

  assign not_1_out = ~B;  // NOT_Gate not_1, 32 bits wide
  Multiplexer #(.width(32), .enable("false")) multiplexer_1 (
    .in0(B), .in1(not_1_out), .out(multiplexer_1_out), .sel(Binv));
  Adder #(.width(32)) adder_1 (.a(A), .b(multiplexer_1_out), .out(adder_1_out), .cin(Cin), .cout(Cout));
  assign nand_1_out = ~(A & B);  // NAND_Gate nand_1, 32 bits wide
  Multiplexer #(.width(32), .enable("false")) multiplexer_2 (
    .in0(adder_1_out), .in1(nand_1_out), .out(AluOut), .sel(AluOp));
  Comparator #(.width(32), .mode("unsigned")) comparator_1 (.a({32{1'b0}}), .b(AluOut), .eq(Z));  // open: gt, lt
endmodule

module R_type_Datapath (
  input  PCEnable,
  input  Clock,
  input  Clear,
  input  Write_Control,
  input  Clear_2,
  input  Cin,
  input  Binv
);

  wire [2:0] rom_1_data_2;
  wire [7:0] adder_1_out, PC_q;
  wire [31:0] n8_32_bit_register_file_1_read_data_1, n8_32_bit_register_file_1_read_data_2,
       n32_bit_alu_1_aluout, rom_1_data;

  Register PC (.D(adder_1_out), .en(PCEnable), .Q(PC_q), .clk(Clock), .clr(Clear));
  Adder adder_1 (.a(8'h1), .b(PC_q), .out(adder_1_out), .cin(1'b0));  // open: cout
  ROM #(.dataWidth(32)) rom_1 (.addr(PC_q), .data({rom_1_data[31:23], rom_1_data_2, rom_1_data[19:0]}));  // open: sel
  _8_32_bit_Register_File u_8_32_bit_register_file_1 (
    .Write_Data(n32_bit_alu_1_aluout), .Read_Data_1(n8_32_bit_register_file_1_read_data_1),
    .Read_Data_2(n8_32_bit_register_file_1_read_data_2), .rd(rom_1_data[28:26]), .Clock(Clock),
    .Clear(Clear_2), .Write_Control(Write_Control), .rs(rom_1_data[25:23]), .rt(rom_1_data_2));
  _32_bit_ALU u_32_bit_alu_1 (
    .Cin(Cin), .Binv(Binv), .AluOut(n32_bit_alu_1_aluout), .A(n8_32_bit_register_file_1_read_data_1),
    .B(n8_32_bit_register_file_1_read_data_2), .AluOp(rom_1_data[29]));  // open: Cout, Z

  // Notes on the sheet:
  //   Instruction Memory
  //   contents of rom_1 (hex, n*v repeats v):
  //   0 1ea00000
  //   rt
  //   rs
  //   rd
  //   opcode
endmodule
