// Logisim project ALU.circ as structural Verilog: 2 circuits, main circuit Alu1Bit
module Alu1Bit (
  input  A,
  input  B,
  input  Cin,
  input  AluOp,
  output AluOut,
  output Cout
);

  wire adder_1_out, nand_1_out;

  Adder #(.width(1)) adder_1 (.a(A), .b(B), .out(adder_1_out), .cin(Cin), .cout(Cout));
  nand nand_1 (nand_1_out, A, B);
  Multiplexer multiplexer_1 (.in0(adder_1_out), .in1(nand_1_out), .out(AluOut), .sel(AluOp));
endmodule

module Alu32Bit (
  input  [31:0] A,
  input  [31:0] B,
  input  Cin,
  input  AluOp,
  output [31:0] AluOut,
  output Cout
);

  wire a0_cout, a1_cout, a2_cout, a3_cout, a4_cout, a5_cout, a6_cout, a7_cout, a8_cout, a9_cout, a10_cout,
       a11_cout, a12_cout, a13_cout, a14_cout, a15_cout, a16_cout, a17_cout, a18_cout, a19_cout, a20_cout,
       a21_cout, a22_cout, a23_cout, a24_cout, a25_cout, a26_cout, a27_cout, a28_cout, a29_cout, a30_cout;

  Alu1Bit a31 (.A(A[31]), .B(B[31]), .Cin(a30_cout), .AluOp(AluOp), .AluOut(AluOut[31]), .Cout(Cout));
  Alu1Bit a23 (.A(A[23]), .B(B[23]), .Cin(a22_cout), .AluOp(AluOp), .AluOut(AluOut[23]), .Cout(a23_cout));
  Alu1Bit a15 (.A(A[15]), .B(B[15]), .Cin(a14_cout), .AluOp(AluOp), .AluOut(AluOut[15]), .Cout(a15_cout));
  Alu1Bit a7 (.A(A[7]), .B(B[7]), .Cin(a6_cout), .AluOp(AluOp), .AluOut(AluOut[7]), .Cout(a7_cout));
  Alu1Bit a30 (.A(A[30]), .B(B[30]), .Cin(a29_cout), .AluOp(AluOp), .AluOut(AluOut[30]), .Cout(a30_cout));
  Alu1Bit a22 (.A(A[22]), .B(B[22]), .Cin(a21_cout), .AluOp(AluOp), .AluOut(AluOut[22]), .Cout(a22_cout));
  Alu1Bit a14 (.A(A[14]), .B(B[14]), .Cin(a13_cout), .AluOp(AluOp), .AluOut(AluOut[14]), .Cout(a14_cout));
  Alu1Bit a6 (.A(A[6]), .B(B[6]), .Cin(a5_cout), .AluOp(AluOp), .AluOut(AluOut[6]), .Cout(a6_cout));
  Alu1Bit a29 (.A(A[29]), .B(B[29]), .Cin(a28_cout), .AluOp(AluOp), .AluOut(AluOut[29]), .Cout(a29_cout));
  Alu1Bit a21 (.A(A[21]), .B(B[21]), .Cin(a20_cout), .AluOp(AluOp), .AluOut(AluOut[21]), .Cout(a21_cout));
  Alu1Bit a13 (.A(A[13]), .B(B[13]), .Cin(a12_cout), .AluOp(AluOp), .AluOut(AluOut[13]), .Cout(a13_cout));
  Alu1Bit a5 (.A(A[5]), .B(B[5]), .Cin(a4_cout), .AluOp(AluOp), .AluOut(AluOut[5]), .Cout(a5_cout));
  Alu1Bit a28 (.A(A[28]), .B(B[28]), .Cin(a27_cout), .AluOp(AluOp), .AluOut(AluOut[28]), .Cout(a28_cout));
  Alu1Bit a20 (.A(A[20]), .B(B[20]), .Cin(a19_cout), .AluOp(AluOp), .AluOut(AluOut[20]), .Cout(a20_cout));
  Alu1Bit a12 (.A(A[12]), .B(B[12]), .Cin(a11_cout), .AluOp(AluOp), .AluOut(AluOut[12]), .Cout(a12_cout));
  Alu1Bit a4 (.A(A[4]), .B(B[4]), .Cin(a3_cout), .AluOp(AluOp), .AluOut(AluOut[4]), .Cout(a4_cout));
  Alu1Bit a27 (.A(A[27]), .B(B[27]), .Cin(a26_cout), .AluOp(AluOp), .AluOut(AluOut[27]), .Cout(a27_cout));
  Alu1Bit a19 (.A(A[19]), .B(B[19]), .Cin(a18_cout), .AluOp(AluOp), .AluOut(AluOut[19]), .Cout(a19_cout));
  Alu1Bit a11 (.A(A[11]), .B(B[11]), .Cin(a10_cout), .AluOp(AluOp), .AluOut(AluOut[11]), .Cout(a11_cout));
  Alu1Bit a3 (.A(A[3]), .B(B[3]), .Cin(a2_cout), .AluOp(AluOp), .AluOut(AluOut[3]), .Cout(a3_cout));
  Alu1Bit a26 (.A(A[26]), .B(B[26]), .Cin(a25_cout), .AluOp(AluOp), .AluOut(AluOut[26]), .Cout(a26_cout));
  Alu1Bit a18 (.A(A[18]), .B(B[18]), .Cin(a17_cout), .AluOp(AluOp), .AluOut(AluOut[18]), .Cout(a18_cout));
  Alu1Bit a10 (.A(A[10]), .B(B[10]), .Cin(a9_cout), .AluOp(AluOp), .AluOut(AluOut[10]), .Cout(a10_cout));
  Alu1Bit a2 (.A(A[2]), .B(B[2]), .Cin(a1_cout), .AluOp(AluOp), .AluOut(AluOut[2]), .Cout(a2_cout));
  Alu1Bit a25 (.A(A[25]), .B(B[25]), .Cin(a24_cout), .AluOp(AluOp), .AluOut(AluOut[25]), .Cout(a25_cout));
  Alu1Bit a17 (.A(A[17]), .B(B[17]), .Cin(a16_cout), .AluOp(AluOp), .AluOut(AluOut[17]), .Cout(a17_cout));
  Alu1Bit a9 (.A(A[9]), .B(B[9]), .Cin(a8_cout), .AluOp(AluOp), .AluOut(AluOut[9]), .Cout(a9_cout));
  Alu1Bit a1 (.A(A[1]), .B(B[1]), .Cin(a0_cout), .AluOp(AluOp), .AluOut(AluOut[1]), .Cout(a1_cout));
  Alu1Bit a24 (.A(A[24]), .B(B[24]), .Cin(a23_cout), .AluOp(AluOp), .AluOut(AluOut[24]), .Cout(a24_cout));
  Alu1Bit a16 (.A(A[16]), .B(B[16]), .Cin(a15_cout), .AluOp(AluOp), .AluOut(AluOut[16]), .Cout(a16_cout));
  Alu1Bit a8 (.A(A[8]), .B(B[8]), .Cin(a7_cout), .AluOp(AluOp), .AluOut(AluOut[8]), .Cout(a8_cout));
  Alu1Bit a0 (.A(A[0]), .B(B[0]), .Cin(Cin), .AluOp(AluOp), .AluOut(AluOut[0]), .Cout(a0_cout));
endmodule
