// Logisim project Datapath.circ as structural Verilog: 2 circuits, main circuit InstructionFetchUnit
module InstructionFetchUnit (
  input  PCEnable,
  input  Clock,
  input  Clear,
  output [31:0] Instruction
);

  wire [7:0] adder_1_out, PC_q;

  Register PC (.D(adder_1_out), .en(PCEnable), .clk(Clock), .Q(PC_q), .clr(Clear));
  ROM #(.dataWidth(32)) InstructionMemory (.addr(PC_q), .data(Instruction));
  Adder adder_1 (.a(8'h1), .b(PC_q), .out(adder_1_out));  // open: cin, cout

  // Notes on the sheet:
  //   Instruction Memory
endmodule

module rType (
  input  Enable,
  input  Clock,
  input  Clear
);

  wire not_1_out;
  wire [31:0] alu32bit_1_aluout, instructionfetchunit_1_instruction, registerfile_1_readdata1,
       registerfile_1_readdata2;

  InstructionFetchUnit instructionfetchunit_1 (
    .PCEnable(Enable), .Clock(Clock), .Clear(Clear), .Instruction(instructionfetchunit_1_instruction));
  not not_1 (not_1_out, instructionfetchunit_1_instruction[29]);
  RegisterFile registerfile_1 (
    .rs(instructionfetchunit_1_instruction[25:23]), .rt(instructionfetchunit_1_instruction[22:20]),
    .rd(instructionfetchunit_1_instruction[28:26]), .WriteData(alu32bit_1_aluout), .Clear(Clear),
    .Clock(Clock), .RegWrite(1'b1), .ReadData1(registerfile_1_readdata1), .ReadData2(registerfile_1_readdata2));
  Alu32Bit alu32bit_1 (
    .A(registerfile_1_readdata1), .B(registerfile_1_readdata2), .Cin(1'b0), .AluOp(not_1_out),
    .AluOut(alu32bit_1_aluout));  // open: Cout

  // Notes on the sheet:
  //   rt
  //   rs
  //   rd
  //   opcode
endmodule
