// Logisim project RegisterFile.circ as structural Verilog: 1 circuit, main circuit RegisterFile
module RegisterFile (
  input  [31:0] WriteData,
  input  [2:0] rs,
  input  Clear,
  input  Clock,
  input  [2:0] rt,
  input  RegWrite,
  input  [2:0] rd,
  output [31:0] ReadData1,
  output [31:0] ReadData2
);

  wire and_1_out, and_2_out, and_3_out, and_4_out, and_5_out, and_6_out, and_7_out, and_8_out,
       decoder_1_out0, decoder_1_out1, decoder_1_out2, decoder_1_out3, decoder_1_out4, decoder_1_out5,
       decoder_1_out6, decoder_1_out7;
  wire [31:0] r0_q, r1_q, r2_q, r3_q, r4_q, r5_q, r6_q, r7_q;

  Decoder #(.enable("false"), .select(3)) decoder_1 (
    .out0(decoder_1_out0), .out1(decoder_1_out1), .out2(decoder_1_out2), .out3(decoder_1_out3),
    .out4(decoder_1_out4), .out5(decoder_1_out5), .out6(decoder_1_out6), .out7(decoder_1_out7), .sel(rd));
  Register #(.width(32)) r7 (.D(WriteData), .en(and_1_out), .clk(Clock), .Q(r7_q), .clr(Clear));
  and and_1 (and_1_out, decoder_1_out7, RegWrite);
  Register #(.width(32)) r6 (.D(WriteData), .en(and_2_out), .clk(Clock), .Q(r6_q), .clr(Clear));
  and and_2 (and_2_out, decoder_1_out6, RegWrite);
  Register #(.width(32)) r5 (.D(WriteData), .en(and_3_out), .clk(Clock), .Q(r5_q), .clr(Clear));
  and and_3 (and_3_out, decoder_1_out5, RegWrite);
  Register #(.width(32)) r4 (.D(WriteData), .en(and_4_out), .clk(Clock), .Q(r4_q), .clr(Clear));
  and and_4 (and_4_out, decoder_1_out4, RegWrite);
  and and_5 (and_5_out, decoder_1_out3, RegWrite);
  Register #(.width(32)) r3 (.D(WriteData), .en(and_5_out), .clk(Clock), .Q(r3_q), .clr(Clear));
  and and_6 (and_6_out, decoder_1_out2, RegWrite);
  Register #(.width(32)) r2 (.D(WriteData), .en(and_6_out), .clk(Clock), .Q(r2_q), .clr(Clear));
  Register #(.width(32)) r1 (.D(WriteData), .en(and_7_out), .clk(Clock), .Q(r1_q), .clr(Clear));
  and and_7 (and_7_out, decoder_1_out1, RegWrite);
  Register #(.width(32)) r0 (.D(WriteData), .en(and_8_out), .clk(Clock), .Q(r0_q), .clr(Clear));
  and and_8 (and_8_out, decoder_1_out0, RegWrite);
  Multiplexer #(.select(3), .width(32)) multiplexer_1 (
    .in0(r0_q), .in1(r1_q), .in2(r2_q), .in3(r3_q), .in4(r4_q), .in5(r5_q), .in6(r6_q), .in7(r7_q),
    .out(ReadData1), .sel(rs));
  Multiplexer #(.select(3), .width(32)) multiplexer_2 (
    .in0(r0_q), .in1(r1_q), .in2(r2_q), .in3(r3_q), .in4(r4_q), .in5(r5_q), .in6(r6_q), .in7(r7_q),
    .out(ReadData2), .sel(rt));
endmodule
